# Fritzing sketch Sesle Çalışan Motor Devre (saved by Fritzing 0.9.3b)
breadboards: 1

parts:
  Part1 = Arduino Uno (Rev3)
  R1 = Resistor [tolerance=±5% resistance=330 package="0603 [SMD]"]
  M1 = DC Motor
  Q1 = NPN-Transistor [package="TO92 [THT]"]

nets:
  N1: Part1.D5_PWM, R1.Pin_1
  N2: Part1.5V, M1.pin_2
  N3: Part1.GND, Q1.C
  N4: R1.Pin_0, Q1.B
  N5: M1.pin_1, Q1.E
