# Fritzing sketch hareket_Dedektoru (saved by Fritzing 0.9.3b)
breadboards: 1

parts:
  part = HC-SR501 Body Sensor Module
  Arduino_UNO = Arduino Uno (Rev3)
  J1 = Basic Servo

nets:
  VCC: part.VCC, Arduino_UNO.5V, J1.vcc
  N1: part.OUT, Arduino_UNO.D8
  GND: part.GND, Arduino_UNO.GND, J1.gnd
  N2: Arduino_UNO.D9_PWM, J1.pulse

custom parts:
  HC-SR501 Body Sensor Module: Pyroelectric Infrared PIR Motion Sensor Detector Module
