# Fritzing sketch RTC Saat (saved by Fritzing 0.9.3b)
breadboards: 1

parts:
  Parça2 = Arduino Uno (Rev3) - ICSP
  U3 = LCD-16X2 [package=lcd-16x2_noholes]
  U4 = POT [package=pot_mammoth]
  PCB2 = RTC_DS1302_module

nets:
  N1: Parça2.ICSP_MISO, Parça2.D12/MISO, U3.RS
  N2: Parça2.D8, PCB2.RST
  N3: Parça2.D11_PWM/MOSI, U3.E
  N4: Parça2.D2, U3.DB7
  N5: Parça2.D3_PWM, U3.DB6
  N6: Parça2.D4, U3.DB5
  N7: Parça2.D5_PWM, U3.DB4
  N8: Parça2.D6_PWM, PCB2.CLK
  N9: Parça2.D7, PCB2.DAT
  5V: Parça2.5V, U3.VDD, U3.A, U4.E, PCB2.VCC
  GND: Parça2.GND, U3.VSS, U3.R_W, U3.K, U4.S, PCB2.GND
  N10: U3.VO, U4.A

custom parts:
  RTC_DS1302_module: Arduino module DS1302 SPI Real Time Clock
