# Fritzing sketch yagmur sensoru (saved by Fritzing 0.9.3b)
breadboards: 1

parts:
  Parça1 = Arduino Uno (Rev3)
  R1 = Resistor [tolerance=±5% resistance=330 package="1206 [SMD]"]
  J1 = Piezo Speaker
  Water_Level_Sensor1 = Water Level Sensor

nets:
  N1: Parça1.A0, Water_Level_Sensor1.SIG
  N2: Parça1.D8, J1.pin2
  5V: Parça1.5V, Water_Level_Sensor1.VCC
  GND: Parça1.GND, R1.Pin_1, Water_Level_Sensor1.GND
  N3: R1.Pin_0, J1.pin1

custom parts:
  Water Level Sensor: A water level sensor. This sensor operates at 3V to 5V. The Sig (signal) pin outputs an analogue signal that is in proportion to the amount of water in contact with the sensor.
