# Fritzing sketch Arduino_05_Devre_Semasi (saved by Fritzing 0.9.3b)
breadboards: 1

parts:
  Parça1 = Arduino Uno (Rev3)
  LED1 = LED - 5mm [color="Red (633nm)" package="5 mm [THT]"]
  R2 = Resistor [tolerance=±5% resistance=330 package=THT]
  R3 = Rotary Potentiometer (Small) [maximum_resistance=100kΩ package=THT]

nets:
  N1: Parça1.A0, R3.wiper
  N2: Parça1.D3_PWM, R2.Pin_1
  N3: Parça1.5V, R3.leg2
  N4: Parça1.GND, LED1.cathode, R3.leg1
  N5: LED1.anode, R2.Pin_0
