# Fritzing sketch Arduino_06 Karasimsek Devre Semasi (saved by Fritzing 0.9.3b)
breadboards: 1

parts:
  Part1 = Arduino Uno (Rev3)
  R1 = Resistor [tolerance=±5% resistance=330 package=THT]
  R2 = Resistor [tolerance=±5% resistance=330 package=THT]
  R3 = Resistor [tolerance=±5% resistance=330 package=THT]
  R4 = Resistor [tolerance=±5% resistance=330 package=THT]
  R5 = Resistor [tolerance=±5% resistance=330 package=THT]
  R6 = Resistor [tolerance=±5% resistance=330 package=THT]
  LED1 = LED - 5mm [color="Red (633nm)" package="5 mm [THT]"]
  LED2 = LED - 5mm [color="Red (633nm)" package="5 mm [THT]"]
  LED3 = LED - 5mm [color="Red (633nm)" package="5 mm [THT]"]
  LED4 = LED - 5mm [color="Red (633nm)" package="5 mm [THT]"]
  LED5 = LED - 5mm [color="Red (633nm)" package="5 mm [THT]"]
  LED6 = LED - 5mm [color="Red (633nm)" package="5 mm [THT]"]

nets:
  N1: Part1.GND, LED2.cathode, LED4.cathode, LED6.cathode
  N2: Part1.D2, R1.Pin_1
  N3: Part1.D3_PWM, R6.Pin_1
  N4: Part1.D4, R5.Pin_1
  N5: Part1.D5_PWM, R4.Pin_1
  N6: Part1.D6_PWM, R3.Pin_1
  N7: Part1.D7, R2.Pin_1
  N8: R1.Pin_0, LED6.anode
  N9: R2.Pin_0, LED1.anode
  N10: R3.Pin_0, LED2.anode
  N11: R4.Pin_0, LED3.anode
  N12: R5.Pin_0, LED4.anode
  N13: R6.Pin_0, LED5.anode
