# Fritzing sketch Arduino_09_NTC (saved by Fritzing 0.9.3b)
breadboards: 1

parts:
  Part1 = Arduino Uno (Rev3)
  R1 = Temperature Sensor (Thermistor) [thermistor_type=NTC package=THT]
  R2 = Resistor [tolerance=±5% resistance=10k package="0805 [SMD]"]
  LED1 = LED - 5mm [color="Red (633nm)" package="5 mm [THT]"]
  R3 = Resistor [tolerance=±5% resistance=10k package="0805 [SMD]"]

nets:
  N1: Part1.A0, R1.pin_0, R2.Pin_1
  N2: Part1.D2, R3.Pin_1
  N3: Part1.5V, R1.pin_1
  N4: Part1.GND, R2.Pin_0, LED1.cathode
  N5: LED1.anode, R3.Pin_0
