# Fritzing sketch LM35 Sicaklik Olcumu (saved by Fritzing 0.9.3b)
breadboards: 1

parts:
  Part1 = Arduino Uno (Rev3)
  J1 = Piezo Speaker
  LED1 = LED - 5mm [color="Red (633nm)" package="5 mm [THT]"]
  T1 = LM35 Temperature Sensor [package="TO92 [THT]"]
  R1 = Resistor [tolerance=±5% resistance=330 package=THT]
  R2 = Resistor [tolerance=±5% resistance=330 package=THT]

nets:
  N1: Part1.A0, T1.Vout
  N2: Part1.D8, R2.Pin_1
  N3: Part1.D9_PWM, R1.Pin_1
  GND: Part1.GND, J1.pin1, LED1.cathode, T1.GND
  N4: Part1.5V, T1.+Vs
  N5: J1.pin2, R1.Pin_0
  N6: LED1.anode, R2.Pin_0
