# Fritzing sketch Boy_olcer_sema (saved by Fritzing 0.9.3b)

parts:
  Parça1 = Arduino Nano (Rev3.0)
  LCD1 = LCD screen
  hc-sr1 = hc-sr04
  S1 = Pushbutton [package="[THT]"]
  R2 = Rotary Potentiometer (Small) [maximum_resistance=100kΩ package=THT]
  R1 = Resistor [tolerance=±5% resistance=220 package=THT]

nets:
  N1: Parça1.D2, LCD1.DB7
  N2: Parça1.D3, LCD1.DB6
  N3: Parça1.D4, LCD1.DB5
  N4: Parça1.D5, LCD1.DB4
  N5: Parça1.D6, S1.Pin_4, R1.Pin_1
  N6: Parça1.D7, hc-sr1.Echo
  N7: Parça1.D8, hc-sr1.Trig
  N8: Parça1.D11/MOSI, LCD1.E
  N9: Parça1.D12/MISO, LCD1.RS
  N10: LCD1.VSS, LCD1.LED-
  N11: LCD1.VDD, LCD1.LED+
  N12: LCD1.V0, R2.wiper
