# Fritzing sketch NRF24_RX (saved by Fritzing 0.9.3b)

parts:
  Part4 = Arduino Uno (Rev3)
  Part5 = NRF24L01+ Breakout Board

nets:
  N1: Part4.D9_PWM, Part5.CE
  N2: Part4.D10_PWM/SS, Part5.CS
  N3: Part4.D11_PWM/MOSI, Part5.MOSI
  N4: Part4.D12/MISO, Part5.MISO
  N5: Part4.D13/SCK, Part5.SCK
  GND: Part4.GND, Part5.GND
  3V3: Part4.3V3, Part5.VCC
