# Fritzing sketch nrf24 verici (saved by Fritzing 0.9.3b)
breadboards: 1

parts:
  Part1 = NRF24L01+ Breakout Board
  Part2 = Arduino Uno (Rev3)
  Part3 = InvenSense MPU6050
  U1 = LIPO-1000mAh [package=lipo-1000]

nets:
  GND: Part1.GND, Part2.GND, Part3.GND, U1.-
  VCC: Part1.VCC, Part2.3V3
  N1: Part1.CE, Part2.D9_PWM
  N2: Part1.CS, Part2.D10_PWM/SS
  N3: Part1.SCK, Part2.D13/SCK
  N4: Part1.MOSI, Part2.D11_PWM/MOSI
  N5: Part1.MISO, Part2.D12/MISO
  N6: Part2.A4/SDA, Part3.SDA
  N7: Part2.A5/SCL, Part3.SCL
  N8: Part3.VCC, U1.+
