# Fritzing sketch bluetooth rgb (saved by Fritzing 0.9.3b)
breadboards: 1

parts:
  LED1 = RGB LED (com. cathode, rgb) [package="5 mm [THT]"]
  Parça1 = Arduino Uno (Rev3) - ICSP
  R2 = Resistor [tolerance=±5% resistance=330 package="2512 [SMD]"]
  R3 = Resistor [tolerance=±5% resistance=330 package="2512 [SMD]"]
  R4 = Resistor [tolerance=±5% resistance=330 package="2512 [SMD]"]
  BT1 = Bluetooth HC-06u [package=THT]

nets:
  N1: LED1.red_anode, R4.Pin_1
  5V: LED1.common_cathode, Parça1.5V, BT1.VCC
  N2: LED1.green_anode, R3.Pin_1
  N3: LED1.blue_anode, R2.Pin_1
  N4: Parça1.D9_PWM, R4.Pin_0
  N5: Parça1.D10_PWM/SS, R3.Pin_0
  N6: Parça1.D11_PWM/MOSI, R2.Pin_0
  N7: Parça1.D0/RX, BT1.TXD
  N8: Parça1.D1/TX, BT1.RXD
  GND: Parça1.GND, BT1.GND

notes:
  Setin içindeki bluetooth modülünde "State" ve "Key" pinleri bulunmamaktadır. Sadece 4 adet pin bağlantısı yapılacaktır.

custom parts:
  Bluetooth HC-06u: Bluetooth HC-06 - face up, pins down 16.5mm x 37.5mm PCB
